# Fritzing sketch ESP8266 18650 (saved by Fritzing 0.9.6b)

parts:
  TP1 = TP4056 [chip_label=TP4056 package="DIP (Dual Inline) [THT]"]
  U1 = ESP8266-07 [part_number=ESP8266]
  18650_holder1 = 18650 holder [package="DIP (Dual Inline) [THT]"]
  S1 = Momentary Switch [package=ksa_sealed_tac_switch]

nets:
  N1: TP1.pin3, U1.VCC
  N2: TP1.pin4, 18650_holder1.holder_+
  N3: TP1.pin5, 18650_holder1.holder_-
  N4: TP1.pin6, U1.GND, S1.2
  N5: U1.GPIO_0, S1.4

custom parts:
  TP4056: A DIP stand-in part for whatever IC you want. With 6 pins on a 300mil dual inline package (DIP) footprint.
  ESP8266-07: ESP8266 - 07 WiFi Module on PCB
  18650 holder: Акум формата 18650 в холдере
